# Fritzing sketch laser control synap.sys (saved by Fritzing 0.8.7b)
circuit board: 1cm x 1cm
circuit board: 6.9215cm x 5.33756cm
breadboards: 1

parts:
  J1 = Basic Servo
  J2 = Basic Servo
  Power_plug1 = Power plug
  J3 = Basic Servo
  J4 = Basic Servo
  J5 = male pin header, 3 pins [form="♂ (male)"]
  U1 = Voltage Regulator - 5V [package="TO220 [THT]"]
  J6 = male pin header, 3 pins [form="♂ (male)"]
  J7 = male pin header, 3 pins [form="♂ (male)"]
  J8 = male pin header, 3 pins [form="♂ (male)"]
  Q2 = MOSFET-NCHANNEL [package=to-92]
  Q3 = MOSFET-NCHANNEL [package=to-92]
  Q4 = MOSFET-NCHANNEL [package=to-92]
  R1 = Resistor [tolerance=±5% resistance=5k package=THT]
  R2 = Resistor [tolerance=±5% resistance=5k package=THT]
  R3 = Resistor [tolerance=±5% resistance=5k package=THT]
  J9 = Basic Servo
  J10 = male pin header, 3 pins [form="♂ (male)"]
  Q5 = MOSFET-NCHANNEL [package=to-92]
  R5 = Resistor [tolerance=±5% resistance=5k package=THT]
  U3 = Voltage Regulator - Variable [package="TO220 [THT]"]
  C1 = Ceramic Capacitor [capacitance=100nF package="100 mil [THT, multilayer]"]
  C2 = Ceramic Capacitor [capacitance=100nF package="100 mil [THT, multilayer]"]
  C3 = Ceramic Capacitor [capacitance=100nF package="100 mil [THT, multilayer]"]
  R6 = Resistor [tolerance=±5% resistance=240 package=THT]
  R7 = Resistor [tolerance=±5% resistance=330 package=THT]
  Q1 = MOSFET-NCHANNEL [package=to-92]
  R8 = Resistor [tolerance=±5% resistance=5k package=THT]
  R9 = Resistor [tolerance=±5% resistance=330k package=THT]
  R10 = Resistor [tolerance=±5% resistance=330k package=THT]
  R11 = Resistor [tolerance=±5% resistance=330k package=THT]
  R12 = Resistor [tolerance=±5% resistance=330k package=THT]
  R13 = Resistor [tolerance=±5% resistance=330k package=THT]
  Q6 = Basic FET N-Channel [package="TO220 [THT]"]
  Q7 = Basic FET N-Channel [package="TO220 [THT]"]
  Q8 = Basic FET N-Channel [package="TO220 [THT]"]
  Q9 = Basic FET N-Channel [package="TO220 [THT]"]
  Q10 = Basic FET N-Channel [package="TO220 [THT]"]
  Componente1 = Arduino Uno (Rev3)
  D1 = Rectifier Diode [part_number=1N4001 package="300 mil [THT]"]
  R14 = Resistor [tolerance=±5% resistance=90 package=THT]
  LED1 = LED - 3mm [color="Red (633nm)" package="3 mm [THT]"]
  R15 = Resistor [tolerance=±5% resistance=90 package=THT]
  LED2 = LED - 3mm [color="Red (633nm)" package="3 mm [THT]"]
  J11 = female pin header, 3 pins [form="♀ (female)"]
  R16 = Resistor [tolerance=±5% resistance=2k package=THT]
  SW1 = DIP SWITCH [package=dipswitch-02]
  R17 = Resistor [tolerance=±5% resistance=5.6k package=THT]
  R18 = Temperature Sensor (Thermistor) [thermistor_type=NTC package=THT]
  R19 = Resistor [tolerance=±5% resistance=10k package=THT]
  R20 = Temperature Sensor (Thermistor) [thermistor_type=NTC package=THT]
  R21 = Resistor [tolerance=±5% resistance=10k package=THT]
  U4 = Voltage Regulator - Variable [package="TO220 [THT]"]
  R22 = Resistor [tolerance=±5% resistance=3 power=1W package=THT]
  R23 = Resistor [tolerance=±5% resistance=3 package=THT]
  U5 = Voltage Regulator - Variable [package="TO220 [THT]"]  # not connected

nets:
  GND/GND_LASER/GND_Servo: J1.gnd, J2.gnd, Power_plug1.GND, J3.gnd, J4.gnd, J5.pin2, U1.GND, J6.pin2, J7.pin2, J8.pin2, Q2.S, Q3.S, Q4.S, J9.gnd, J10.pin2, Q5.S, C1.0, C2.1, C3.1, R7.Pin_0, Q1.S, R9.Pin_0, R10.Pin_0, R11.Pin_0, R12.Pin_0, R13.Pin_0, Q6.source, Q7.source, Q8.source, Q9.source, Q10.source, Componente1.GND, LED1.cathode, LED2.cathode, J11.pin2, R19.Pin_0, R21.Pin_0
  5V_-_Servos: J1.vcc, J2.vcc, J3.vcc, J4.vcc, U1.output_voltage, J9.vcc, C1.1
  Signal_2_Servo: J1.pulse, Componente1.D9_PWM
  Signal_1_Servo: J2.pulse, Componente1.D8
  N1: Power_plug1.VCC, D1.anode
  Signal_3_Servo: J3.pulse, Componente1.D10_PWM/SS
  Signal_4_Servo: J4.pulse, Componente1.D11_PWM/MOSI
  3.3V_Laser: J5.pin1, J6.pin1, J7.pin1, J8.pin1, J10.pin1, C2.0, R6.Pin_1, R15.Pin_0, J11.pin1, R16.Pin_1, R17.Pin_1, R22.Pin_1, R23.Pin_1
  Sinal_out_5_laser: J5.pin3, Q1.D, Q6.drain, J11.pin3
  N2: U1.input_voltage, U3.IN, C3.0, D1.cathode, U4.IN
  N3: J6.pin3, Q2.D, Q7.drain
  N4: J7.pin3, Q3.D, Q8.drain
  N5: J8.pin3, Q4.D, Q9.drain
  N6: Q2.G, R3.Pin_0, R11.Pin_1, Q7.gate
  N7: Q3.G, R2.Pin_0, R10.Pin_1, Q8.gate
  N8: Q4.G, R1.Pin_0, R9.Pin_1, Q9.gate
  Sinal_2_Laser: R1.Pin_1, Componente1.D3_PWM
  Sinal_4_Laser: R2.Pin_1, Componente1.D4
  Sinal_3_Laser: R3.Pin_1, Componente1.D5_PWM
  Signal_5_Servo: J9.pulse, Componente1.D12/MISO
  N9: J10.pin3, Q5.D, Q10.drain
  N10: Q5.G, R5.Pin_0, R13.Pin_1, Q10.gate
  Sinal_1_Laser: R5.Pin_1, Componente1.D2
  N11: U3.ADJ, R6.Pin_0, R7.Pin_1, SW1.3, SW1.4, U4.ADJ
  N12: U3.OUT, R22.Pin_0
  N13: Q1.G, R8.Pin_0, R12.Pin_1, Q6.gate
  Sinal_5_Laser: R8.Pin_1, Componente1.D6_PWM, R14.Pin_0
  Termo Sensor Laser: Componente1.A0, R18.pin_0, R19.Pin_1
  Termo Sensor Servo: Componente1.A1, R20.pin_0, R21.Pin_1
  5V: Componente1.5V, R18.pin_1, R20.pin_1
  N14: R14.Pin_1, LED1.anode
  N15: R15.Pin_1, LED2.anode
  N16: R16.Pin_0, SW1.2
  N17: SW1.1, R17.Pin_0
  N18: U4.OUT, R23.Pin_0
